# Fritzing sketch new design 3 final schematic (saved by Fritzing 0.9.3b)
circuit board: 9cm x 6.5cm
breadboards: 1

parts:
  Fuse1 = Fuse with Handler [part_number=Htc-15m]
  header_4 = Header 4 [package=screwterminal-3.5mm-4_lock]
  header_4_2 = Header 4 [package=screwterminal-3.5mm-4_lock]
  MPU6050 = MPU-6050 Board GY-521 [form="♀ (female)" package=THT]
  J1 = screw terminal, 2 pins
  A4988 = A4988 Stepper Motor Driver Carrier
  arduino_nano_1 = Arduino Nano (Rev3.0)
  U5v1 = Voltage Regulator - 5V [package="TO220 [THT]"]
  C4 = Electrolytic Capacitor [capacitance=100µF package="200 mil [THT, electrolytic]"]
  C5 = Capacitor Polarized [package=cpol-radial-10uf-25v]
  C6 = Capacitor Polarized [package=cpol-radial-10uf-25v]  # not connected
  U3 = SWITCH-SPST-2 [package=switch-spst-vertical]
  A4988_2 = A4988 Stepper Motor Driver Carrier

nets:
  N1: Fuse1.Connector1, U3.P
  N2: header_4.1, A4988.OUT_1B
  N3: header_4.2, A4988.OUT_1A
  N4: header_4.3, A4988.OUT_2A
  N5: header_4.4, A4988.OUT_2B
  N6: header_4_2.1, A4988_2.OUT_1B
  N7: header_4_2.2, A4988_2.OUT_1A
  N8: header_4_2.3, A4988_2.OUT_2A
  N9: header_4_2.4, A4988_2.OUT_2B
  VDD: MPU6050.pin1, A4988.VDD, arduino_nano_1.5V, U5v1.output_voltage, A4988_2.VDD
  N10: MPU6050.pin2, J1.pin2, A4988.GROUND, arduino_nano_1.GND, C4.-, C5.-, A4988_2.GROUND
  N11: MPU6050.pin3, arduino_nano_1.A5
  N12: MPU6050.pin4, arduino_nano_1.A4
  N13: A4988.RESET, A4988.SLEEP
  N14: A4988.STEP, arduino_nano_1.D5
  N15: A4988.DIR, arduino_nano_1.D4
  N16: arduino_nano_1.D6, A4988_2.DIR
  N17: arduino_nano_1.D7, A4988_2.STEP
  N18: arduino_nano_1.D10, A4988_2.MS3
  N19: arduino_nano_1.D11/MOSI, A4988_2.MS2
  N20: arduino_nano_1.D12/MISO, A4988_2.MS1
  N21: U5v1.input_voltage, C5.+, A4988_2.VMOT
  N22: C4.+, U3.O
  N23: A4988_2.RESET, A4988_2.SLEEP

custom parts:
  MPU-6050 Board GY-521: Acelerometro y Giroscopio MPU-6050 Board GY-521
